# Fritzing sketch Arduino_Basic (saved by Fritzing 0.9.3b)
breadboards: 1

parts:
  Componente1 = Arduino Uno (Rev3)
  RHT1 = Humidity and Temperature Sensor RHT03
  R1 = Photocell (LDR) [package=THT]
  R2 = Resistor [tolerance=±5% resistance=220 package=THT]
  T1 = LM35 Temperature Sensor [package="TO92 [THT]"]
  T2 = LM35 Temperature Sensor [package="TO92 [THT]"]

nets:
  N1: Componente1.A0, RHT1.GND_1
  N2: Componente1.A1, RHT1.Data-signal
  N3: Componente1.A2, R1.pin_0, R2.Pin_1
  N4: Componente1.D2, T1.+Vs
  N5: Componente1.D4, T2.+Vs
  5V: Componente1.5V, RHT1.Vcc, R1.pin_1, T1.Vout, T2.Vout
  GND: Componente1.GND, RHT1.GND_2, R2.Pin_0, T1.GND, T2.GND
