# Fritzing sketch a1_shield-e_1-relay (saved by Fritzing 0.9.3b)

parts:
  Part1 = Arduino Uno (Rev3)  # not connected
  Part2 = Arduino Ethernet Shield (Rev3)
  U1 = 2-Channel 5v Relay Shield [package=relay-2ch5v10a]
  Raspberry_Pi_1 = Raspberry Pi 3 [part_number=RPI-3-V1.2]  # not connected

nets:
  N1: Part2.PWM_D5, U1.VCC
  N2: Part2.PWM_D6, U1.IN1
  N3: Part2.D7, U1.GND

custom parts:
  2-Channel 5v Relay Shield: 2 Channel 5v Relay Shield w. 2x SPD-06VDC-SD-C
