# Fritzing sketch schema di montaggio (saved by Fritzing 0.9.3b)
breadboards: 1

parts:
  Componente1 = Arduino Yun
  U1 = G3VM-61E1 [package=g3vm-61e1]
  U2 = G3VM-61E1 [package=g3vm-61e1]
  S1 = Pushbutton [package="[SMD]"]
  S2 = Pushbutton [package="[SMD]"]
  J2 = Basic Servo
  J1 = Basic Servo
  R2 = Resistor [tolerance=±5% resistance=330 package="0805 [SMD]"]
  R1 = Resistor [tolerance=±1% resistance=330 package="0603 [SMD]"]
  R3 = Temperature Sensor (Thermistor) [thermistor_type=NTC package=THT]
  R4 = Resistor [tolerance=±1% resistance=100k package="0805 [SMD]"]
  R5 = PHOTOCELL [package=photocell-kit]
  R6 = Resistor [tolerance=±1% resistance=100k package="0603 [SMD]"]

nets:
  N1: Componente1.A0, R5.P$2, R6.Pin_0
  N2: Componente1.A1, R3.pin_1, R4.Pin_1
  VCC: Componente1.5V, U1.P$1, U2.P$1, S1.Pin_3, S1.Pin_4, S2.Pin_3, S2.Pin_4, J2.vcc, J1.vcc, R3.pin_0, R5.P$1
  N3: Componente1.GND, U1.P$3, U2.P$3, R2.Pin_1, R1.Pin_1, R4.Pin_0, R6.Pin_1
  N4: Componente1.D10_PWM/SS, J1.pulse
  N5: Componente1.D11_PWM/MOSI, J2.pulse
  N6: Componente1.D12/MISO, U1.P$2
  N7: Componente1.D13/SCK, U2.P$2
  N8: Componente1.D5_PWM, S1.Pin_1, S1.Pin_2, R1.Pin_0
  GND: Componente1.D6_PWM, S2.Pin_1, S2.Pin_2, J2.gnd, J1.gnd, R2.Pin_0

notes:
  Light Relays and Light Buttons
  Light and Temperature Sensor
  Curtains servo motors
