# Fritzing sketch schema di montaggio (saved by Fritzing 0.9.3b)
breadboards: 1

parts:
  Componente1 = Arduino Yun
  S1 = Pushbutton [package="[SMD]"]
  S2 = Pushbutton [package="[SMD]"]
  R2 = Resistor [tolerance=±5% resistance=330 package="0805 [SMD]"]
  R1 = Resistor [tolerance=±1% resistance=330 package="0603 [SMD]"]
  R3 = Temperature Sensor (Thermistor) [thermistor_type=NTC package=THT]
  R4 = Resistor [tolerance=±1% resistance=100k package="0805 [SMD]"]
  R5 = PHOTOCELL [package=photocell-kit]
  R6 = Resistor [tolerance=±1% resistance=100k package="0603 [SMD]"]
  LED1 = smd LED [color="Red (633nm)" package="0603 [SMD]"]
  LED2 = smd LED [color="Red (633nm)" package="1206 [SMD]"]
  R7 = Resistor [tolerance=±5% resistance=220 package="0402 [SMD]"]
  R8 = Resistor [tolerance=±5% resistance=220 package="0402 [SMD]"]

nets:
  N1: Componente1.A0, R5.P$2, R6.Pin_0
  N2: Componente1.A1, R3.pin_1, R4.Pin_1
  N3: Componente1.GND, R2.Pin_1, R1.Pin_1, R4.Pin_0, R6.Pin_1, LED1.cathode, LED2.cathode
  N4: Componente1.D12/MISO, R7.Pin_1
  N5: Componente1.D13/SCK, R8.Pin_1
  N6: Componente1.D5_PWM, S1.Pin_1, S1.Pin_2, R1.Pin_0
  N7: Componente1.D6_PWM, S2.Pin_1, S2.Pin_2, R2.Pin_0
  N8: Componente1.5V, S1.Pin_3, S1.Pin_4, S2.Pin_3, S2.Pin_4, R3.pin_0, R5.P$1
  N9: LED1.anode, R8.Pin_0
  N10: LED2.anode, R7.Pin_0

notes:
  Light Relays and Light Buttons
  Light and Temperature Sensor
  Curtains servo motors
